# Fritzing sketch Fritzing_sketch (saved by Fritzing 0.9.3b)
circuit board: 6.97174cm x 4.10415cm
breadboards: 1

parts:
  U2 = atmega328 [package=dip]
  C2 = Ceramic Capacitor [capacitance=22pF package="100 mil [THT, multilayer]"]
  C3 = Ceramic Capacitor [capacitance=22pF package="100 mil [THT, multilayer]"]
  C4 = Ceramic Capacitor [capacitance=22µF package="100 mil [THT, multilayer]"]
  R1 = Resistor [tolerance=±5% resistance=10k package=THT]
  Q1 = NPN-Transistor [package="TO92 [THT]"]
  Serial = female pin header, 6 pins [form="♀ (female)"]
  Y1 = CRYSTAL [package=hc49u-v]
  LEDS = female pin header, 4 pins [form="♀ (female)"]
  D1 = Rectifier Diode [part_number=1N4001 package="300 mil [THT]"]
  R2 = Resistor [tolerance=±5% resistance=220 package=THT]
  ETHERNET = double row female pin header, 10 pins [form="♀ (female)"]
  C5 = Electrolytic Capacitor [capacitance=47µF package="100 mil [THT, electrolytic]"]

nets:
  N1: U2.RESET, C4.0, R1.Pin_1
  N2: U2.D0_(RX), Serial.pin4
  N3: U2.D1_(TX), Serial.pin5
  N4: U2.D2, ETHERNET.pin1
  N5: U2.D3_(PWM), R2.Pin_0
  5V: U2.VCC, U2.AVCC, R1.Pin_0, D1.cathode, ETHERNET.pin6, C5.+
  GND: U2.GND, C2.1, C3.1, Serial.pin1, LEDS.pin3, ETHERNET.pin5, C5.-
  N6: U2.XLAT1, C2.0, Y1.2
  N7: U2.XLAT2, C3.0, Y1.1
  N8: U2.D9_(PWM), ETHERNET.pin4
  N9: U2.D10_(PWM), ETHERNET.pin7
  N10: U2.D11_(PWM), LEDS.pin2, ETHERNET.pin8
  N11: U2.D12, ETHERNET.pin2
  N12: U2.D13, Q1.E, ETHERNET.pin3
  N13: C4.1, Serial.pin6
  N14: Q1.B, R2.Pin_1
  N15: Q1.C, LEDS.pin1
  N16: LEDS.pin4, D1.anode

notes:
  CLK DT GRD 5V
